// Logisim project SequentialDivider.circ as structural Verilog: 1 circuit, main circuit Divider
module Divider (
  input  [3:0] Dividend,
  input  [3:0] Divisor,
  input  RESET,
  output [3:0] Quotient,
  output [3:0] Remainder,
  output DONE
);


  // Notes on the sheet:
  //   First name LAST NAME, Student Number
endmodule
