// Logisim project led.circ as structural Verilog: 1 circuit, main circuit main
module main (
);

  wire undriven, undriven_2, undriven_3, undriven_4, undriven_5, undriven_6, undriven_7, undriven_8,
       undriven_9, undriven_10;

  Clock clock_1 ();  // open: out
  LED led_1 (.in(undriven));
  LED led_2 (.in(undriven_2));
  LED led_3 (.in(undriven_3));
  LED led_4 (.in(undriven_5));
  LED led_5 (.in(undriven_4));
  LED led_6 (.in(undriven_6));
  LED led_7 (.in(undriven_7));
  LED led_8 (.in(undriven_8));
  LED led_9 (.in(undriven_9));
  LED led_10 (.in(undriven_10));

  // Notes on the sheet:
  //   1
  //   0
  //   2
  //   3
  //   First name LAST NAME, Student Number
  //   5
  //   4
  //   6
  //   7
  //   8
  //   9
endmodule
